// Digital circuit Computer.dig as structural Verilog
module Computer (
  input  CLK
);

  wire cpu_1_wrt, RESET_out;
  wire [4:0] gpu_1_row;
  wire [5:0] gpu_1_addr;
  wire [8:0] bitextender_1_out;
  wire [14:0] cpu_1_addr, cpu_1_pc;
  wire [15:0] cpu_1_dout, ramdualaccess_1_d1, ramdualaccess_1_d2, rom_1_d;
  wire [31:0] gpu_1_dout;

  Button RESET (.out(RESET_out));
  BitExtender #(.inputBits(1), .outputBits(9)) bitextender_1 (.in(1'b1), .out(bitextender_1_out));
  ROM #(.AddrBits(15), .isProgramMemory("true"), .Bits(16)) rom_1 (.A(cpu_1_pc), .sel(1'b1), .D(rom_1_d));
  CPU cpu_1 (
    .DIN(ramdualaccess_1_d1), .INS(rom_1_d), .CLK(CLK), .CLR(RESET_out), .DOUT(cpu_1_dout), .WRT(cpu_1_wrt),
    .ADDR(cpu_1_addr), .PC(cpu_1_pc));
  RAMDualAccess #(.AddrBits(15), .Bits(16)) ramdualaccess_1 (
    .str(cpu_1_wrt), .C(CLK), .ld(1'b1), .A1(cpu_1_addr), .Din1(cpu_1_dout),
    .A2({bitextender_1_out, gpu_1_addr}), .D1(ramdualaccess_1_d1), .D2(ramdualaccess_1_d2));
  GPU gpu_1 (
    .DIN(ramdualaccess_1_d2), .CLK(CLK), .CLR(RESET_out), .DOUT(gpu_1_dout), .ADDR(gpu_1_addr),
    .ROW(gpu_1_row));
  LedMatrix #(.ledPersistence("true"), .colAddrBits(5), .rowDataBits(32)) ledmatrix_1 (
    .rows(gpu_1_dout), .column(gpu_1_row));

  // Notes on the sheet:
  //   CLK: Hz: 2147483647
endmodule
